# Fritzing sketch pilightmodul (saved by Fritzing 0.9.3b)
circuit board: 5.16113cm x 2.85044cm
breadboards: 1

parts:
  U1 = attiny85 [package=dip]
  R1 = Resistor [tolerance=±5% resistance=1k package=THT]
  R2 = Resistor [tolerance=±5% resistance=1k package=THT]
  R3 = Resistor [tolerance=±5% resistance=1k package=THT]
  R4 = Resistor [tolerance=±5% resistance=1k package=THT]
  R5 = Resistor [tolerance=±5% resistance=1k package=THT]
  Raspberry_Pi_Zero1 = Raspberry Pi 3 [part_number=RPI-3-V1.2]
  ANT1 = Antenna
  J1 = Dagu DGServo 9g header (male) [package=THT]
  JP3 = Header 4 [package=molex-1x4_lock]
  ANT2 = Antenna
  J$1 = SMA Antenna Connector [package=sma-edge]

nets:
  N1: U1.Pin_1, R1.Pin_0
  N2: U1.Pin_2, R2.Pin_0
  N3: U1.Pin_3, JP3.2
  GND: U1.Pin_4, Raspberry_Pi_Zero1.GND, J1.gnd, JP3.1
  N4: U1.Pin_5, R3.Pin_0
  N5: U1.Pin_6, R4.Pin_0
  N6: U1.Pin_7, R5.Pin_0
  5V: U1.Pin_8, Raspberry_Pi_Zero1.5V, J1.Vcc, JP3.4
  N7: R1.Pin_1, Raspberry_Pi_Zero1.GPIO8
  N8: R2.Pin_1, Raspberry_Pi_Zero1.GPIO18
  N9: R3.Pin_1, Raspberry_Pi_Zero1.GPIO10
  N10: R4.Pin_1, Raspberry_Pi_Zero1.GPIO9
  N11: R5.Pin_1, Raspberry_Pi_Zero1.GPIO11
  N12: Raspberry_Pi_Zero1.GPIO17, J1.pulse
  N13: ANT1.antenna_lead, ANT2.antenna_lead, J$1.SIGNAL

notes:
  REV.A
  receiver
  sender
  GND
  DAT
  VCC
  ANT
