# Fritzing sketch pilightrecv (saved by Fritzing 0.9.3b)
circuit board: 4.12047cm x 1.56799cm
breadboards: 1

parts:
  U1 = attiny85 [package=dip]
  R1 = Resistor [tolerance=±5% resistance=1k package=THT]
  R2 = Resistor [tolerance=±5% resistance=1k package=THT]
  R3 = Resistor [tolerance=±5% resistance=1k package=THT]
  R4 = Resistor [tolerance=±5% resistance=1k package=THT]
  R5 = Resistor [tolerance=±5% resistance=1k package=THT]
  Raspberry_Pi_Zero1 = Raspberry Pi 3 [part_number=RPI-3-V1.2]
  JP1 = Header 2 [package=molex-1x2_lock]
  JP2 = Header 2 [package=molex-1x2_lock]

nets:
  N1: U1.Pin_1, R1.Pin_0
  N2: U1.Pin_2, R2.Pin_0
  N3: U1.Pin_3, JP1.1
  N4: U1.Pin_4, Raspberry_Pi_Zero1.GND, JP1.2
  N5: U1.Pin_5, R3.Pin_0
  N6: U1.Pin_6, R4.Pin_0
  N7: U1.Pin_7, R5.Pin_0
  N8: U1.Pin_8, Raspberry_Pi_Zero1.5V, JP2.1
  N9: R1.Pin_1, Raspberry_Pi_Zero1.GPIO8
  N10: R2.Pin_1, Raspberry_Pi_Zero1.GPIO18
  N11: R3.Pin_1, Raspberry_Pi_Zero1.GPIO10
  N12: R4.Pin_1, Raspberry_Pi_Zero1.GPIO9
  N13: R5.Pin_1, Raspberry_Pi_Zero1.GPIO11

notes:
  pilight
  recv 0.2
